// Logisim project cpu with pipe.circ as structural Verilog: 3 circuits, main circuit Cpu Control
module Cpu_Control (
  input  [5:0] in_1,
  output RegDst,
  output Branch,
  output Jump,
  output MemRead,
  output MemtoReg,
  output [1:0] ALUOp,
  output MemWrite,
  output ALUSrc,
  output RegWrite,
  output Link,
  output beq,
  output bne,
  output bltzal,
  output j,
  output jal,
  output addi,
  output addiu,
  output ori,
  output andi,
  output lui,
  output slti,
  output sltiu
);

  wire comparator_1_eq, comparator_2_eq, comparator_3_eq, or_2_out, or_3_out, or_4_out, or_5_out, or_6_out,
       or_7_out, or_8_out, or_9_out, or_10_out, or_11_out, or_12_out, or_13_out, or_15_out, or_16_out,
       or_18_out, or_19_out, or_20_out, or_21_out, or_22_out, or_23_out, or_24_out, or_25_out, or_26_out,
       or_27_out, or_28_out, or_29_out, or_30_out, or_31_out, or_32_out, or_33_out, or_34_out, or_35_out,
       or_36_out, or_37_out;
  wire [1:0] multiplexer_1_out, multiplexer_2_out, or_1_out;

  Comparator #(.width(6), .mode("unsigned")) comparator_1 (
    .a(in_1), .b({6{1'b0}}), .eq(comparator_1_eq));  // open: gt, lt
  Comparator #(.width(6), .mode("unsigned")) comparator_2 (
    .a(in_1), .b(6'b100011), .eq(comparator_2_eq));  // open: gt, lt
  Comparator #(.width(6), .mode("unsigned")) comparator_3 (
    .a(in_1), .b(6'b101011), .eq(comparator_3_eq));  // open: gt, lt
  Comparator #(.width(6), .mode("unsigned")) comparator_4 (.a(in_1), .b(6'b000100), .eq(beq));  // open: gt, lt
  Comparator #(.width(6), .mode("unsigned")) comparator_5 (.a(in_1), .b(6'b000010), .eq(j));  // open: gt, lt
  Comparator #(.width(6), .mode("unsigned")) comparator_6 (.a(in_1), .b(6'b000011), .eq(jal));  // open: gt, lt
  Comparator #(.width(6), .mode("unsigned")) comparator_7 (.a(in_1), .b(6'b000101), .eq(bne));  // open: gt, lt
  Comparator #(.width(6), .mode("unsigned")) comparator_8 (.a(in_1), .b(6'b000001), .eq(bltzal));  // open: gt, lt
  Comparator #(.width(6), .mode("unsigned")) comparator_9 (.a(in_1), .b(6'b001000), .eq(addi));  // open: gt, lt
  Comparator #(.width(6), .mode("unsigned")) comparator_10 (.a(in_1), .b(6'b001101), .eq(ori));  // open: gt, lt
  Comparator #(.width(6), .mode("unsigned")) comparator_11 (.a(in_1), .b(6'b001111), .eq(lui));  // open: gt, lt
  Comparator #(.width(6), .mode("unsigned")) comparator_12 (.a(in_1), .b(6'b001001), .eq(addiu));  // open: gt, lt
  Comparator #(.width(6), .mode("unsigned")) comparator_13 (.a(in_1), .b(6'b001100), .eq(andi));  // open: gt, lt
  Comparator #(.width(6), .mode("unsigned")) comparator_14 (.a(in_1), .b(6'b001010), .eq(slti));  // open: gt, lt
  Comparator #(.width(6), .mode("unsigned")) comparator_15 (.a(in_1), .b(6'b001011), .eq(sltiu));  // open: gt, lt
  Multiplexer #(.width(2)) multiplexer_1 (
    .in0(2'b00), .in1(2'b01), .out(multiplexer_1_out), .sel(or_3_out));  // open: en
  Multiplexer #(.width(2)) multiplexer_2 (
    .in0(2'b00), .in1(2'b10), .out(multiplexer_2_out), .sel(comparator_1_eq));  // open: en
  assign or_1_out = multiplexer_2_out | multiplexer_1_out;  // OR_Gate or_1, 2 bits wide
  or or_2 (or_2_out, or_6_out, beq, comparator_2_eq, comparator_2_eq, or_4_out, comparator_1_eq);
  or or_3 (or_3_out, beq, or_6_out);
  or or_4 (or_4_out, comparator_3_eq, or_10_out);
  Multiplexer #(.width(2)) multiplexer_3 (.in1(or_1_out), .out(ALUOp), .sel(or_2_out));  // open: in0, en
  or or_5 (or_5_out, 1'b0, comparator_2_eq, jal, comparator_1_eq, or_10_out);
  or or_6 (or_6_out, bne, bltzal);
  or or_7 (or_7_out, 1'b0, comparator_2_eq);
  or or_8 (or_8_out, 1'b0, comparator_2_eq, comparator_3_eq, or_9_out);
  or or_9 (or_9_out, or_12_out, ori, addiu, addi);
  or or_10 (or_10_out, or_11_out, ori, addiu, addi);
  or or_11 (or_11_out, sltiu, slti, andi, lui);
  or or_12 (or_12_out, sltiu, slti, andi, lui);
  buf or_13 (or_13_out, comparator_1_eq);  // OR_Gate
  Multiplexer multiplexer_4 (.in1(or_13_out), .out(RegDst), .sel(or_21_out));  // open: in0, en
  or or_14 (Jump, 1'b0, j, jal);
  Multiplexer multiplexer_5 (.in1(or_15_out), .out(MemRead), .sel(or_22_out));  // open: in0, en
  or or_15 (or_15_out, 1'b0, comparator_2_eq);
  Multiplexer multiplexer_6 (.in1(or_7_out), .out(MemtoReg), .sel(or_23_out));  // open: in0, en
  or or_16 (or_16_out, 1'b0, comparator_3_eq);
  Multiplexer multiplexer_7 (.in1(or_16_out), .out(MemWrite), .sel(or_24_out), .en(or_24_out));  // open: in0
  Multiplexer multiplexer_8 (.in1(or_8_out), .out(ALUSrc), .sel(or_28_out));  // open: in0, en
  Multiplexer multiplexer_9 (.in1(or_5_out), .out(RegWrite), .sel(or_29_out));  // open: in0, en
  or or_17 (Link, 1'b0, or_6_out, jal);
  or or_18 (or_18_out, or_20_out, ori, addiu, addi);
  or or_19 (or_19_out, sltiu, slti, andi, lui);
  or or_20 (or_20_out, sltiu, slti, andi, lui);
  or or_21 (or_21_out, comparator_1_eq, comparator_2_eq, jal, or_33_out);
  or or_22 (or_22_out, beq, comparator_1_eq, comparator_2_eq, comparator_3_eq, j, jal, or_6_out, or_34_out);
  or or_23 (or_23_out, comparator_2_eq, comparator_1_eq, comparator_2_eq, or_26_out);
  or or_24 (or_24_out, comparator_3_eq, comparator_1_eq, or_6_out, comparator_2_eq, beq, j, jal, or_25_out);
  or or_25 (or_25_out, or_19_out, ori, addiu, addi);
  or or_26 (or_26_out, or_27_out, ori, addiu, addi);
  or or_27 (or_27_out, sltiu, slti, andi, lui);
  or or_28 (or_28_out, comparator_1_eq, comparator_2_eq, comparator_3_eq, beq, or_6_out, or_18_out);
  or or_29 (or_29_out, beq, comparator_2_eq, comparator_1_eq, comparator_3_eq, j, jal, or_6_out, or_9_out);
  or or_30 (or_30_out, or_31_out, ori, addiu, addi);
  or or_31 (or_31_out, sltiu, slti, andi, lui);
  or or_32 (or_32_out, sltiu, slti, andi, lui);
  or or_33 (or_33_out, or_35_out, ori, addiu, addi);
  or or_34 (or_34_out, or_32_out, ori, addiu, addi);
  or or_35 (or_35_out, sltiu, slti, andi, lui);
  or or_36 (or_36_out, 1'b0, beq, or_6_out);
  Multiplexer multiplexer_10 (.in1(or_36_out), .out(Branch), .sel(or_37_out));  // open: in0, en
  or or_37 (or_37_out, comparator_1_eq, comparator_2_eq, comparator_3_eq, beq, j, or_6_out, or_30_out);

  // Notes on the sheet:
  //   R type
  //   lw
  //   sw
  //   beq
  //   j
  //   jal
  //   bne
  //   bltzal
  //   addi
  //   ori
  //   lui
  //   addiu
  //   andi
  //   slti
  //   sltiu
endmodule

module Alu_control (
  input  [1:0] aluop,
  input  [5:0] funct,
  input  Adds,
  input  Or,
  input  And,
  input  Lu,
  input  Slt,
  output [3:0] swinc,
  output Jr
);

  wire comparator_1_lt, comparator_2_eq;
  wire [0:0] comparator_3_eq;
  wire [1:1] comparator_4_eq;
  wire [2:2] comparator_1_eq, comparator_5_eq, comparator_6_eq, comparator_7_eq;
  wire [3:0] multiplexer_3_out, or_1_out;
  wire [3:3] comparator_8_eq, comparator_9_eq, comparator_10_eq, comparator_11_eq, comparator_12_eq;
  wire [5:0] multiplexer_1_out;

  Comparator #(.width(2), .mode("unsigned")) comparator_1 (
    .a(2'b01), .b(aluop), .eq(comparator_1_eq[2]), .lt(comparator_1_lt));  // open: gt
  Multiplexer #(.width(6)) multiplexer_1 (
    .in0({6{1'b0}}), .in1(funct), .out(multiplexer_1_out), .sel(comparator_1_lt));  // open: en
  Comparator #(.width(6)) comparator_2 (.a({6{1'b0}}), .b(multiplexer_1_out), .eq(comparator_2_eq));  // open: gt, lt
  Comparator #(.width(6)) comparator_3 (.a(6'b000010), .b(multiplexer_1_out), .eq(comparator_3_eq[0]));  // open: gt, lt
  Comparator #(.width(6)) comparator_4 (.a(6'b000011), .b(multiplexer_1_out), .eq(comparator_4_eq[1]));  // open: gt, lt
  Comparator #(.width(6)) comparator_5 (.a(6'b100000), .b(multiplexer_1_out), .eq(comparator_5_eq[2]));  // open: gt, lt
  Comparator #(.width(6)) comparator_6 (.a(6'b100001), .b(multiplexer_1_out), .eq(comparator_6_eq[2]));  // open: gt, lt
  Comparator #(.width(6)) comparator_7 (.a(6'b100010), .b(multiplexer_1_out), .eq(comparator_7_eq[2]));  // open: gt, lt
  Comparator #(.width(6)) comparator_8 (.a(6'b100011), .b(multiplexer_1_out), .eq(comparator_8_eq[3]));  // open: gt, lt
  Comparator #(.width(6)) comparator_9 (.a(6'b100100), .b(multiplexer_1_out), .eq(comparator_9_eq[3]));  // open: gt, lt
  Comparator #(.width(6)) comparator_10 (
    .a(6'b100101), .b(multiplexer_1_out), .eq(comparator_10_eq[3]));  // open: gt, lt
  Comparator #(.width(6)) comparator_11 (
    .a(6'b101010), .b(multiplexer_1_out), .eq(comparator_11_eq[3]));  // open: gt, lt
  Comparator #(.width(6)) comparator_12 (
    .a(6'b101011), .b(multiplexer_1_out), .eq(comparator_12_eq[3]));  // open: gt, lt
  assign or_1_out = {3'b000, comparator_3_eq[0]} | {2'b00, comparator_4_eq[1], 1'b0} | {1'b0, comparator_5_eq[2], 1'b0, comparator_5_eq[2]} | {1'b0, {2{comparator_6_eq[2]}}, 1'b0} | {1'b0, {3{comparator_7_eq[2]}}} | {comparator_8_eq[3], 3'b000} | {comparator_9_eq[3], 2'b00, comparator_9_eq[3]} | {comparator_10_eq[3], 1'b0, comparator_10_eq[3], 1'b0} | {{3{comparator_11_eq[3]}}, 1'b0} | {4{comparator_12_eq[3]}};  // OR_Gate or_1, 4 bits wide
  Comparator #(.width(6)) comparator_13 (.a(6'b001000), .b(multiplexer_1_out), .eq(Jr));  // open: gt, lt
  Multiplexer #(.select(2), .width(4)) multiplexer_2 (
    .in0(multiplexer_3_out), .in1({1'b0, {3{comparator_1_eq[2]}}}), .in2(or_1_out), .out(swinc), .sel(aluop));  // open: in3, en
  Multiplexer #(.select(5), .width(4)) multiplexer_3 (
    .in0(4'b0101), .in1(4'b1110), .in2(4'b0101), .in4(4'b1001), .in8(4'b1010), .in16(4'b0101),
    .out(multiplexer_3_out), .sel({Adds, Or, And, Lu, Slt}));  // open: in3, in5, in6, in7, in9, in10, in11, in12, in13, in14, in15, in17, in18, in19, in20, in21, in22, in23, in24, in25, in26, in27, in28, in29, in30, in31, en

  // Other names for the same wires on the sheet: Itype[4:0] = {Adds, Or, And, Lu, Slt}
endmodule

module pipe_control (
  input  in_1,
  output [1:0] out_2
);

  wire comparator_1_eq;
  wire [1:0] adder_1_out, multiplexer_1_out;

  Adder #(.width(2)) adder_1 (.a(2'b01), .b(out_2), .out(adder_1_out));  // open: cin, cout
  Multiplexer #(.width(2)) multiplexer_1 (
    .in0(adder_1_out), .in1(2'b00), .out(multiplexer_1_out), .sel(comparator_1_eq));  // open: en
  Comparator #(.width(2)) comparator_1 (.a(2'b01), .b(out_2), .eq(comparator_1_eq));  // open: gt, lt
  Register #(.width(2)) register_1 (.D(multiplexer_1_out), .Q(out_2), .clk(in_1));  // open: en, clr
endmodule
