// Logisim project cpu.circ as structural Verilog: 1 circuit, main circuit main
module main (
  input  [31:0] INSTRUCTION,
  input  CLOCK,
  output [31:0] FETCH_ADDRESS,
  output [31:0] s0_Value,
  output [31:0] s1_Value,
  output [31:0] s2_Value,
  output [31:0] ra_Value,
  output [31:0] sp_Value
);

  wire and_1_out, main_2_equal;
  wire [4:0] multiplexer_1_out, undriven;
  wire [31:0] adder_1_out, adder_2_out, bit_extender_1_out, main_1_read_data_1, main_1_read_data_2,
       main_2_result, main_3_p3, multiplexer_2_out, multiplexer_3_out, multiplexer_4_out, multiplexer_5_out,
       shifter_2_out;

  Register #(.width(32)) PC (.D(multiplexer_4_out), .Q(FETCH_ADDRESS));  // open: en, clk, clr
  Adder #(.width(32)) adder_1 (.a(32'h4), .b(FETCH_ADDRESS), .out(adder_1_out));  // open: cin, cout
  Shifter #(.width(26)) shifter_1 (.in(INSTRUCTION[25:0]), .\dist (5'b00010), .out(adder_1_out[25:0]));
  Multiplexer #(.width(5)) multiplexer_1 (
    .in0(undriven), .in1(INSTRUCTION[15:11]), .out(multiplexer_1_out));  // open: sel, en
  regfile_main main_1 (
    .Read_Register_1(INSTRUCTION[25:21]), .Read_Register_2(undriven), .Write_Register(multiplexer_1_out),
    .Write_Data(multiplexer_5_out), .Read_Data_1(main_1_read_data_1), .Read_Data_2(main_1_read_data_2),
    .s0_Value(s0_Value), .s1_Value(s1_Value), .s2_Value(s2_Value), .ra_Value(ra_Value), .sp_Value(sp_Value));  // open: Write_Enable, Clock
  assign bit_extender_1_out = {{16{INSTRUCTION[15]}}, INSTRUCTION[15:0]};  // Bit_Extender bit_extender_1
  Demultiplexer #(.width(6)) demultiplexer_1 (.in(INSTRUCTION[5:0]));  // open: out0, out1, sel, en
  Shifter #(.width(32)) shifter_2 (.in(bit_extender_1_out), .\dist (5'b00010), .out(shifter_2_out));
  Adder #(.width(32)) adder_2 (.a(adder_1_out), .b(shifter_2_out), .out(adder_2_out));  // open: cin, cout
  Multiplexer #(.width(32)) multiplexer_2 (
    .in0(main_1_read_data_2), .in1(bit_extender_1_out), .out(multiplexer_2_out));  // open: sel, en
  Multiplexer #(.width(32)) multiplexer_3 (
    .in0(adder_1_out), .in1(adder_2_out), .out(multiplexer_3_out));  // open: sel, en
  alu_main main_2 (
    .X(main_1_read_data_1), .Equal(main_2_equal), .Result(main_2_result), .Y(multiplexer_2_out));  // open: Switch, Signed_Overflow
  Multiplexer #(.width(32)) multiplexer_4 (
    .in0(adder_1_out), .in1(multiplexer_3_out), .out(multiplexer_4_out), .sel(and_1_out));  // open: en
  buf and_1 (and_1_out, main_2_equal);  // AND_Gate
  // mem_main main_3: pin names not known; wires that end beside it: main_2_result, main_1_read_data_2, main_3_p3
  Multiplexer #(.width(32)) multiplexer_5 (
    .in0(main_3_p3), .in1(main_2_result), .out(multiplexer_5_out));  // open: sel, en
  // Pins of 26 and 32 bits meet at adder_1_out

  // Other names for the same wires on the sheet: clk = CLOCK; fetch_addr[31:0] = FETCH_ADDRESS; ra[31:0] = ra_Value;
  //   s0[31:0] = s0_Value; s1[31:0] = s1_Value; s2[31:0] = s2_Value; sp[31:0] = sp_Value

  // Notes on the sheet:
  //   Output
  //   These are outputs/inputs from run.circ
  //   Inputs
  //   These are DEBUG/TEST outputs from your circuit.
endmodule
